# Fritzing sketch circuit (saved by Fritzing 0.9.3b)
breadboards: 1

parts:
  Raspberry_Pi_Zero_W = Raspberry Pi Zero
  R1 = Resistor [tolerance=±5% resistance=339 package="1206 [SMD]"]
  R2 = Resistor [tolerance=±5% resistance=100 package="1206 [SMD]"]
  R3 = Resistor [tolerance=±5% resistance=100 package="1206 [SMD]"]
  RGB_LED = RGB LED - (4 legs) [package="5 mm [THT]"]
  PIR_Motion_Sensor = PIR sensor
  Buzzer = Piezo Speaker

nets:
  N1: Raspberry_Pi_Zero_W.pin_2, Raspberry_Pi_Zero_W.pin_4, PIR_Motion_Sensor.GND, Buzzer.pin1
  N2: Raspberry_Pi_Zero_W.pin_6, Raspberry_Pi_Zero_W.pin_9, Raspberry_Pi_Zero_W.pin_34, RGB_LED.common_anode, PIR_Motion_Sensor.VDD
  N3: Raspberry_Pi_Zero_W.pin_11, R1.Pin_0
  N4: Raspberry_Pi_Zero_W.pin_12, Buzzer.pin2
  N5: Raspberry_Pi_Zero_W.pin_13, R2.Pin_1
  N6: Raspberry_Pi_Zero_W.pin_15, R3.Pin_1
  N7: Raspberry_Pi_Zero_W.pin_16, PIR_Motion_Sensor.SIG
  N8: R1.Pin_1, RGB_LED.red_cathode
  N9: R2.Pin_0, RGB_LED.green_cathode
  N10: R3.Pin_0, RGB_LED.blue_cathode

notes:
  Pi Compatible Camera
